# Fritzing sketch Esquema Circuito (saved by Fritzing 0.9.3b)
breadboards: 1

parts:
  IR1 = TSOP312.., 314.. [package=THT]
  LED1 = LED - 5mm [color="Red (633nm)" package="5 mm [THT]"]
  R1 = Resistor [tolerance=±5% resistance=220 package="0402 [SMD]"]
  R3 = Resistor [tolerance=±5% resistance=20k package="2010 [SMD]"]
  R4 = Resistor [tolerance=±5% resistance=20k package="0603 [SMD]"]
  R5 = Resistor [tolerance=±5% resistance=20k package="2010 [SMD]"]
  R6 = Resistor [tolerance=±5% resistance=10k package="2010 [SMD]"]
  R8 = Resistor [tolerance=±5% resistance=20k package="2010 [SMD]"]
  R7 = Resistor [tolerance=±5% resistance=10k package="2010 [SMD]"]
  U2 = ESP8266 WiFi Module [part_number=ESP8266]
  Pro_Micro1 = SparkFun Pro Micro
  J1 = Infrared Proximity Sensor

nets:
  N1: IR1.GND, U2.GPIO_2, Pro_Micro1.2
  N2: IR1.Vs, LED1.cathode, R1.Pin_0
  VCC: IR1.Data, LED1.anode, R3.Pin_1, Pro_Micro1.VCC, J1.Vcc
  GND: R1.Pin_1, R4.Pin_0, R5.Pin_1, R8.Pin_1, U2.GND, J1.GND
  N3: R3.Pin_0, R4.Pin_1, U2.VCC
  N4: R5.Pin_0, R6.Pin_1, U2.TXD
  N5: R6.Pin_0, Pro_Micro1.RX1
  N6: R8.Pin_0, R7.Pin_1, U2.RXD
  N7: R7.Pin_0, Pro_Micro1.TX0
  N8: Pro_Micro1.3, J1.Vout

notes:
  Sensor de proximidade básico
  Módulo sensor de proximidade

custom parts:
  ESP8266 WiFi Module: Generic WiFi Module based on the ESP8266 with onboard PCB antenna and UART communications
  SparkFun Pro Micro: The Pro Micro is similar to the Pro Mini except with an ATmega32U4 on board. The USB transceiver inside the 32U4 allows us to add USB connectivity on-board and do away with bulky external USB interface. Based on: https://github.com/unorthodox-engineers/unorthodox-arduino/blob/master/Unorthodox/fritzing/parts/Pro%20Micro.fzpz
